// Logisim project ex1.circ as structural Verilog: 4 circuits, main circuit NOR1
module NOR1 (
  input  A,
  input  B,
  output RESULT
);

  wire and_1_out;

  and and_1 (and_1_out, A, B);
  not not_1 (RESULT, and_1_out);

  // Notes on the sheet:
  //   PUT CIRCUITRY HERE
endmodule

module XOR1 (
  input  A,
  input  B,
  output RESULT
);

  wire and_1_out, and_2_out, not_1_out, not_2_out;

  not not_1 (not_1_out, A);
  not not_2 (not_2_out, B);
  and and_1 (and_1_out, not_1_out, B);
  and and_2 (and_2_out, A, not_2_out);
  or or_1 (RESULT, and_1_out, and_2_out);

  // Notes on the sheet:
  //   PUT CIRCUITRY HERE
endmodule

module MUX2 (
  input  A,
  input  Sel,
  input  B,
  output RESULT
);

  wire and_1_out, and_2_out, not_1_out;

  not not_1 (not_1_out, Sel);
  and and_1 (and_1_out, A, not_1_out);
  and and_2 (and_2_out, Sel, B);
  or or_1 (RESULT, and_1_out, and_2_out);

  // Notes on the sheet:
  //   PUT CIRCUITRY HERE
endmodule

module MUX4 (
  input  A,
  input  B,
  input  C,
  input  D,
  input  Sel2,
  input  Sel1,
  output RESULT
);

  wire and_1_out, and_2_out, and_3_out, and_4_out, not_1_out, not_2_out;

  not not_1 (not_1_out, Sel2);
  not not_2 (not_2_out, Sel1);
  and and_1 (and_1_out, A, not_1_out, not_2_out);
  and and_2 (and_2_out, B, not_1_out, Sel1);
  and and_3 (and_3_out, C, Sel2, not_2_out);
  and and_4 (and_4_out, D, Sel2, Sel1);
  or or_1 (RESULT, and_1_out, and_2_out, and_3_out, and_4_out);

  // Notes on the sheet:
  //   PUT CIRCUITRY HERE
endmodule
